// Logisim project Calculadora 16 bits.circ as structural Verilog: 11 circuits, main circuit main
module main (
  input  Subtrair,
  input  [15:0] \Número_1 ,
  input  [15:0] \Número_2 
);

  wire a0, a1, a2, a3, a4, a5, a6, a7, a8, a9, aa, ab, ac, b0, b1, b2, b3, b4, b5, b6, b7, b8, b9, ba, bb,
       bc, c0, c1, c2, c3, c4, c5, c6, c7, c8, c9, ca, cb, cc, d0, d1, d2, d3, d4, d5, d6, d7, d8, d9, da,
       db, dc, e0, e1_t, e2_t, e3, e4, e5, e6, e7, e8, e9, ea, eb, ec, f0, f1, f2, f3, f4, f5, f6, f7, f8,
       f9, fa, fb, fc, g0, g1, g2, g3, g4, g5, g6, g7, g8, g9, ga, gb, gc, R,
       somador_completo_16_bits_1_c_out;
  wire [4:0] sinal_matriz_5x5_1_s0, sinal_matriz_5x5_1_s1, sinal_matriz_5x5_1_s2, sinal_matriz_5x5_1_s3,
       sinal_matriz_5x5_1_s4, switch_matriz_5x5_1_s0, switch_matriz_5x5_1_s1, switch_matriz_5x5_1_s2,
       switch_matriz_5x5_1_s3, switch_matriz_5x5_1_s4;
  wire [15:0] inversor_controlado_16_bits_1_s, S;

  xor xor_1 (R, Subtrair, somador_completo_16_bits_1_c_out);
  Hexadecimal__para_7_segmentos hexadecimal_para_7_segmentos_1 (
    .E(\Número_1 [15:12]), .A(a0), .B(b0), .C(c0), .D(d0), .E_2(e0), .F(f0), .G(g0));
  Somador_Completo_16_bits somador_completo_16_bits_1 (
    .A(\Número_1 ), .B(inversor_controlado_16_bits_1_s), .C_in(Subtrair), .S(S),
    .C_out(somador_completo_16_bits_1_c_out));
  Hexadecimal__para_7_segmentos hexadecimal_para_7_segmentos_2 (
    .E(\Número_1 [11:8]), .A(a1), .B(b1), .C(c1), .D(d1), .E_2(e1_t), .F(f1), .G(g1));
  Inversor_Controlado_16_bits inversor_controlado_16_bits_1 (
    .H(Subtrair), .E(\Número_2 ), .S(inversor_controlado_16_bits_1_s));
  Hexadecimal__para_7_segmentos hexadecimal_para_7_segmentos_3 (
    .E(\Número_1 [7:4]), .A(a2), .B(b2), .C(c2), .D(d2), .E_2(e2_t), .F(f2), .G(g2));
  Resto_para_7_segmentos resto_para_7_segmentos_1 (.in_1(R), .A(ac), .B(bc), .C(cc), .D(dc), .E(ec), .F(fc), .G(gc));
  _7_Segment_Display u_7_segment_display_1 (.g(g0), .f(f0), .a(a0), .b(b0), .e(e0), .d(d0), .c(c0));  // open: dp
  Hexadecimal__para_7_segmentos hexadecimal_para_7_segmentos_4 (
    .E(\Número_1 [3:0]), .A(a3), .B(b3), .C(c3), .D(d3), .E_2(e3), .F(f3), .G(g3));
  _7_Segment_Display u_7_segment_display_2 (.g(g1), .f(f1), .a(a1), .b(b1), .e(e1_t), .d(d1), .c(c1));  // open: dp
  _7_Segment_Display u_7_segment_display_3 (.g(g2), .f(f2), .a(a2), .b(b2), .e(e2_t), .d(d2), .c(c2));  // open: dp
  Hexadecimal__para_7_segmentos hexadecimal_para_7_segmentos_5 (
    .E(\Número_2 [15:12]), .A(a4), .B(b4), .C(c4), .D(d4), .E_2(e4), .F(f4), .G(g4));
  _7_Segment_Display u_7_segment_display_4 (.g(g3), .f(f3), .a(a3), .b(b3), .e(e3), .d(d3), .c(c3));  // open: dp
  DotMatrix #(.matrixrows(5)) dotmatrix_1 (
    .col0(switch_matriz_5x5_1_s4), .col1(switch_matriz_5x5_1_s3), .col2(switch_matriz_5x5_1_s2),
    .col3(switch_matriz_5x5_1_s1), .col4(switch_matriz_5x5_1_s0));
  Switch_____matriz_5x5 switch_matriz_5x5_1 (
    .Switch(Subtrair), .S4(switch_matriz_5x5_1_s4), .S3(switch_matriz_5x5_1_s3), .S2(switch_matriz_5x5_1_s2),
    .S1(switch_matriz_5x5_1_s1), .S0(switch_matriz_5x5_1_s0));
  Hexadecimal__para_7_segmentos hexadecimal_para_7_segmentos_6 (
    .E(\Número_2 [11:8]), .A(a5), .B(b5), .C(c5), .D(d5), .E_2(e5), .F(f5), .G(g5));
  _7_Segment_Display u_7_segment_display_5 (.g(g4), .f(f4), .a(a4), .b(b4), .e(e4), .d(d4), .c(c4));  // open: dp
  Hexadecimal__para_7_segmentos hexadecimal_para_7_segmentos_7 (
    .E(\Número_2 [7:4]), .A(a6), .B(b6), .C(c6), .D(d6), .E_2(e6), .F(f6), .G(g6));
  _7_Segment_Display u_7_segment_display_6 (.g(g5), .f(f5), .a(a5), .b(b5), .e(e5), .d(d5), .c(c5));  // open: dp
  _7_Segment_Display u_7_segment_display_7 (.g(g6), .f(f6), .a(a6), .b(b6), .e(e6), .d(d6), .c(c6));  // open: dp
  Hexadecimal__para_7_segmentos hexadecimal_para_7_segmentos_8 (
    .E(\Número_2 [3:0]), .A(a7), .B(b7), .C(c7), .D(d7), .E_2(e7), .F(f7), .G(g7));
  _7_Segment_Display u_7_segment_display_8 (.g(g7), .f(f7), .a(a7), .b(b7), .e(e7), .d(d7), .c(c7));  // open: dp
  DotMatrix #(.matrixrows(5)) dotmatrix_2 (
    .col0(sinal_matriz_5x5_1_s4), .col1(sinal_matriz_5x5_1_s3), .col2(sinal_matriz_5x5_1_s2),
    .col3(sinal_matriz_5x5_1_s1), .col4(sinal_matriz_5x5_1_s0));
  Sinal___matriz_5x5 sinal_matriz_5x5_1 (
    .S4(sinal_matriz_5x5_1_s4), .S3(sinal_matriz_5x5_1_s3), .S2(sinal_matriz_5x5_1_s2),
    .S1(sinal_matriz_5x5_1_s1), .S0(sinal_matriz_5x5_1_s0));
  Hexadecimal__para_7_segmentos hexadecimal_para_7_segmentos_9 (
    .E(S[15:12]), .A(a8), .B(b8), .C(c8), .D(d8), .E_2(e8), .F(f8), .G(g8));
  _7_Segment_Display u_7_segment_display_9 (.g(gc), .f(fc), .a(ac), .b(bc), .e(ec), .d(dc), .c(cc));  // open: dp
  _7_Segment_Display u_7_segment_display_10 (.g(g8), .f(f8), .a(a8), .b(b8), .e(e8), .d(d8), .c(c8));  // open: dp
  Hexadecimal__para_7_segmentos hexadecimal_para_7_segmentos_10 (
    .E(S[11:8]), .A(a9), .B(b9), .C(c9), .D(d9), .E_2(e9), .F(f9), .G(g9));
  _7_Segment_Display u_7_segment_display_11 (.g(ga), .f(fa), .a(aa), .b(ba), .e(ea), .d(da), .c(ca));  // open: dp
  _7_Segment_Display u_7_segment_display_12 (.g(g9), .f(f9), .a(a9), .b(b9), .e(e9), .d(d9), .c(c9));  // open: dp
  Hexadecimal__para_7_segmentos hexadecimal_para_7_segmentos_11 (
    .E(S[7:4]), .A(aa), .B(ba), .C(ca), .D(da), .E_2(ea), .F(fa), .G(ga));
  _7_Segment_Display u_7_segment_display_13 (.g(gb), .f(fb), .a(ab), .b(bb), .e(eb), .d(db), .c(cb));  // open: dp
  Hexadecimal__para_7_segmentos hexadecimal_para_7_segmentos_12 (
    .E(S[3:0]), .A(ab), .B(bb), .C(cb), .D(db), .E_2(eb), .F(fb), .G(gb));

  // Other names for the same wires on the sheet: E1[15:0] = \Número_1 ; E2[15:0] = \Número_2 ; Sub = Subtrair

  // Notes on the sheet:
  //   Entradas e Operador
  //   Controladora de Displays Numero 1
  //   Controladora de Display Resto da Soma
  //   Controladora de Displays Numero 2
  //   Displays e Resultado
  //   Controladora de Displays Resultado
endmodule

// FA
module Somador_Completo (
  input  A,
  input  B,
  input  C_in,
  output S,
  output C_out
);

  wire and_1_out, and_2_out, xor_1_out;

  xor xor_1 (xor_1_out, A, B);
  and and_1 (and_1_out, xor_1_out, C_in);
  and and_2 (and_2_out, A, B);
  xor xor_2 (S, xor_1_out, C_in);
  or or_1 (C_out, and_1_out, and_2_out);

  // Notes on the sheet:
  //   FA
endmodule

// FA 2b
module Somador_Completo_2_bits (
  input  [1:0] A,
  input  [1:0] B,
  input  C_in,
  output [1:0] S,
  output C_out
);

  wire C_in_1;

  Somador_Completo somador_completo_1 (.A(A[0]), .B(B[0]), .C_in(C_in), .S(S[0]), .C_out(C_in_1));
  Somador_Completo somador_completo_2 (.A(A[1]), .B(B[1]), .C_in(C_in_1), .S(S[1]), .C_out(C_out));

  // Other names for the same wires on the sheet: C_in_0 = C_in

  // Notes on the sheet:
  //   FA 2 bits
endmodule

// FA 4b
module Somador_Completo_4_bits (
  input  [3:0] A,
  input  [3:0] B,
  input  C_in,
  output [3:0] S,
  output C_out
);

  wire C_in_1;

  Somador_Completo_2_bits somador_completo_2_bits_1 (.A(A[1:0]), .B(B[1:0]), .C_in(C_in), .S(S[1:0]), .C_out(C_in_1));
  Somador_Completo_2_bits somador_completo_2_bits_2 (.A(A[3:2]), .B(B[3:2]), .C_in(C_in_1), .S(S[3:2]), .C_out(C_out));

  // Other names for the same wires on the sheet: A0[1:0] = A[1:0]; A1[1:0] = A[3:2]; B0[1:0] = B[1:0];
  //   B1[1:0] = B[3:2]; C_in_0 = C_in

  // Notes on the sheet:
  //   FA 4 bits
endmodule

// FA 8b
module Somador_Completo_8_bits (
  input  [7:0] A,
  input  [7:0] B,
  input  C_in,
  output [7:0] S,
  output C_out
);

  wire C_in_1;

  Somador_Completo_4_bits somador_completo_4_bits_1 (.A(A[3:0]), .B(B[3:0]), .C_in(C_in), .S(S[3:0]), .C_out(C_in_1));
  Somador_Completo_4_bits somador_completo_4_bits_2 (.A(A[7:4]), .B(B[7:4]), .C_in(C_in_1), .S(S[7:4]), .C_out(C_out));

  // Other names for the same wires on the sheet: A0[3:0] = A[3:0]; A1[3:0] = A[7:4]; B0[3:0] = B[3:0];
  //   B1[3:0] = B[7:4]; C_in_0 = C_in

  // Notes on the sheet:
  //   FA 8 bits
endmodule

// FA 16b
module Somador_Completo_16_bits (
  input  [15:0] A,
  input  [15:0] B,
  input  C_in,
  output [15:0] S,
  output C_out
);

  wire C_in_1;

  Somador_Completo_8_bits somador_completo_8_bits_1 (.A(A[7:0]), .B(B[7:0]), .C_in(C_in), .S(S[7:0]), .C_out(C_in_1));
  Somador_Completo_8_bits somador_completo_8_bits_2 (
    .A(A[15:8]), .B(B[15:8]), .C_in(C_in_1), .S(S[15:8]), .C_out(C_out));

  // Other names for the same wires on the sheet: A0[7:0] = A[7:0]; A1[7:0] = A[15:8]; B0[7:0] = B[7:0];
  //   B1[7:0] = B[15:8]; C_in_0 = C_in

  // Notes on the sheet:
  //   FA 16 bits
endmodule

// IC 16b
module Inversor_Controlado_16_bits (
  input  [15:0] E,
  input  H,
  output [15:0] S
);

  xor xor_1 (S[15], E[15], H);
  xor xor_2 (S[14], E[14], H);
  xor xor_3 (S[12], E[12], H);
  xor xor_4 (S[13], E[13], H);
  xor xor_5 (S[11], E[11], H);
  xor xor_6 (S[10], E[10], H);
  xor xor_7 (S[8], E[8], H);
  xor xor_8 (S[9], E[9], H);
  xor xor_9 (S[6], H, E[6]);
  xor xor_10 (S[7], H, E[7]);
  xor xor_11 (S[4], H, E[4]);
  xor xor_12 (S[5], H, E[5]);
  xor xor_13 (S[3], H, E[3]);
  xor xor_14 (S[2], H, E[2]);
  xor xor_15 (S[0], H, E[0]);
  xor xor_16 (S[1], H, E[1]);

  // Notes on the sheet:
  //   IC 16b
endmodule

// H27s
module Hexadecimal__para_7_segmentos (
  input  [3:0] E,
  output A,
  output B,
  output C,
  output D,
  output E_2,
  output F,
  output G
);

  wire and_1_out, and_2_out, and_3_out, and_4_out, and_5_out, and_6_out, and_7_out, and_8_out, and_9_out,
       and_10_out, and_11_out, and_12_out, and_13_out, and_14_out, and_15_out, and_16_out, and_17_out,
       and_18_out, and_19_out, and_20_out, and_21_out, and_22_out, and_23_out, and_24_out, and_25_out,
       and_26_out, and_27_out, and_28_out, and_29_out, and_30_out, and_31_out, and_32_out, and_33_out,
       and_34_out, and_35_out, not_1_out, not_2_out, not_3_out, not_4_out;

  not not_1 (not_1_out, E[3]);
  not not_2 (not_2_out, E[2]);
  not not_3 (not_3_out, E[1]);
  not not_4 (not_4_out, E[0]);
  and and_1 (and_1_out, not_4_out, not_2_out);
  and and_2 (and_2_out, E[1], not_1_out);
  and and_3 (and_3_out, E[0], E[2], not_1_out);
  and and_4 (and_4_out, E[1], E[2]);
  and and_5 (and_5_out, not_3_out, not_2_out, E[3]);
  and and_6 (and_6_out, not_4_out, E[3]);
  and and_7 (and_7_out, not_2_out, not_1_out);
  and and_8 (and_8_out, not_4_out, not_3_out, not_1_out);
  and and_9 (and_9_out, not_4_out, not_2_out);
  and and_10 (and_10_out, E[0], E[1], not_1_out);
  and and_11 (and_11_out, E[0], not_3_out, E[3]);
  and and_12 (and_12_out, not_3_out, not_1_out);
  and and_13 (and_13_out, E[0], not_1_out);
  and and_14 (and_14_out, E[0], not_3_out);
  and and_15 (and_15_out, E[2], not_1_out);
  and and_16 (and_16_out, not_2_out, E[3]);
  and and_17 (and_17_out, not_4_out, not_2_out, not_1_out);
  and and_18 (and_18_out, E[0], E[1], not_2_out);
  and and_19 (and_19_out, E[0], not_3_out, E[2]);
  and and_20 (and_20_out, not_4_out, E[1], E[2]);
  and and_21 (and_21_out, not_3_out, E[3]);
  and and_22 (and_22_out, not_4_out, not_2_out);
  and and_23 (and_23_out, not_4_out, E[1]);
  and and_24 (and_24_out, E[1], E[3]);
  and and_25 (and_25_out, E[2], E[3]);
  and and_26 (and_26_out, not_4_out, not_3_out);
  and and_27 (and_27_out, not_3_out, E[2], not_1_out);
  and and_28 (and_28_out, not_4_out, E[2]);
  and and_29 (and_29_out, not_2_out, E[3]);
  and and_30 (and_30_out, E[1], E[3]);
  and and_31 (and_31_out, E[1], not_2_out);
  and and_32 (and_32_out, not_4_out, E[1]);
  and and_33 (and_33_out, not_3_out, E[2], not_1_out);
  and and_34 (and_34_out, not_2_out, E[3]);
  and and_35 (and_35_out, E[0], E[3]);
  or or_1 (A, and_1_out, and_2_out, and_3_out, and_4_out, and_5_out, and_6_out);
  or or_2 (B, and_7_out, and_8_out, and_9_out, and_10_out, and_11_out);
  or or_3 (C, and_12_out, and_13_out, and_14_out, and_15_out, and_16_out);
  or or_4 (D, and_17_out, and_18_out, and_19_out, and_20_out, and_21_out);
  or or_5 (E_2, and_22_out, and_23_out, and_24_out, and_25_out);
  or or_6 (F, and_26_out, and_27_out, and_28_out, and_29_out, and_30_out);
  or or_7 (G, and_31_out, and_32_out, and_33_out, and_34_out, and_35_out);

  // Notes on the sheet:
  //   Hexadecimal para display 7 segmentos
endmodule

// SW M 5x5
module Switch_____matriz_5x5 (
  input  Switch,
  output [4:0] S4,
  output [4:0] S3,
  output [4:0] S2,
  output [4:0] S1,
  output [4:0] S0
);

  not not_1 (S2[4], Switch);
  not not_2 (S0[4], S0[2]);
  xor xor_1 (S0[2], S2[4], Switch);

  assign {S0[3], S0[1:0]} = {3{S0[4]}};
  assign S1 = {{2{S0[4]}}, S0[2], {2{S0[4]}}};
  assign S2[3:0] = {S2[4], S0[2], {2{S2[4]}}};
  assign S3 = {{2{S0[4]}}, S0[2], {2{S0[4]}}};
  assign S4 = {{2{S0[4]}}, S0[2], {2{S0[4]}}};

  // Notes on the sheet:
  //   Circuito para exibir + ou - em uma matriz LED 5x5
endmodule

// S = M 5x5
module Sinal___matriz_5x5 (
  output [4:0] S4,
  output [4:0] S3,
  output [4:0] S2,
  output [4:0] S1,
  output [4:0] S0
);


  assign S0 = 5'b01010;
  assign S1 = 5'b01010;
  assign S2 = 5'b01010;
  assign S3 = 5'b01010;
  assign S4 = 5'b01010;

  // Notes on the sheet:
  //   Circuito para exibir sinel de = em uma matriz LED 5x5
endmodule

// R27s
module Resto_para_7_segmentos (
  input  in_1,
  output A,
  output B,
  output C,
  output D,
  output E,
  output F,
  output G
);

  not not_1 (A, in_1);
  xor xor_1 (B, in_1, A);

  assign C = B;
  assign D = A;
  assign E = A;
  assign F = A;
  assign G = 1'b0;
endmodule
