// Logisim project T22.circ as structural Verilog: 6 circuits, main circuit Latch SR NAND
module Latch_SR_NAND (
  input  S,
  input  H,
  input  R,
  output out_4
);

  wire nand_1_out, nand_2_out, nand_4_out;

  nand nand_1 (nand_1_out, S, H);
  nand nand_2 (nand_2_out, H, R);
  nand nand_3 (out_4, nand_1_out, nand_4_out);
  nand nand_4 (nand_4_out, out_4, nand_2_out);
endmodule

module Latch_SR_NOR (
  input  S,
  input  H,
  input  R,
  output S_2
);

  wire nor_1_out, nor_2_out, nor_4_out, not_1_out;

  not not_1 (not_1_out, H);
  nor nor_1 (nor_1_out, S, not_1_out);
  nor nor_2 (nor_2_out, not_1_out, R);
  nor nor_3 (S_2, nor_1_out, nor_4_out);
  nor nor_4 (nor_4_out, S_2, nor_2_out);
endmodule

module Latch_D (
  input  Q,
  input  H,
  output S1,
  output S2
);

  wire nand_1_out, nand_2_out, not_1_out;

  not not_1 (not_1_out, Q);
  nand nand_1 (nand_1_out, Q, H);
  nand nand_2 (nand_2_out, H, not_1_out);
  nand nand_3 (S1, nand_1_out, S2);
  nand nand_4 (S2, S1, nand_2_out);
endmodule

module Main (
);


  // Notes on the sheet:
  //   T22
  //   Nomes:
  //   Alexsander Luis Gomes
  //   Rafael Nossal
  //   Pedro Fernandes
endmodule

module Flip_Flop_D_Ascendente (
  input  D,
  output S1,
  output S2
);

  wire clock_1_out, nand_1_out, nand_2_out, nand_3_out, nand_4_out;

  Clock clock_1 (.out(clock_1_out));
  nand nand_1 (nand_1_out, nand_4_out, nand_2_out);
  nand nand_2 (nand_2_out, nand_1_out, clock_1_out);
  nand nand_3 (nand_3_out, nand_2_out, clock_1_out, nand_4_out);
  nand nand_4 (nand_4_out, nand_3_out, D);
  nand nand_5 (S1, nand_2_out, S2);
  nand nand_6 (S2, S1, nand_3_out);
endmodule

module Flip_Flop_D_Descendente (
  input  D,
  output S1,
  output S2
);

  wire clock_1_out, nand_1_out, nand_2_out, nand_3_out, nand_4_out, not_1_out;

  Clock clock_1 (.out(clock_1_out));
  not not_1 (not_1_out, clock_1_out);
  nand nand_1 (nand_1_out, nand_4_out, nand_2_out);
  nand nand_2 (nand_2_out, nand_1_out, not_1_out);
  nand nand_3 (nand_3_out, nand_2_out, not_1_out, nand_4_out);
  nand nand_4 (nand_4_out, nand_3_out, D);
  nand nand_5 (S1, nand_2_out, S2);
  nand nand_6 (S2, S1, nand_3_out);
endmodule
