// Logisim project T24.circ as structural Verilog
// REG 1 B
module Exercicio_2 (
  input  Load,
  input  C,
  input  Clear,
  input  D,
  output Q
);

  wire and_1_out, nand_1_out, nand_2_out, nand_3_out, nand_4_out, nand_6_out, not_1_out, not_2_out, or_1_out;

  and and_1 (and_1_out, Load, C);
  or or_1 (or_1_out, Clear, and_1_out);
  not not_1 (not_1_out, Clear);
  not not_2 (not_2_out, Clear);
  nand nand_1 (nand_1_out, nand_4_out, nand_2_out);
  nand nand_2 (nand_2_out, nand_1_out, not_1_out, and_1_out);
  nand nand_3 (nand_3_out, nand_2_out, or_1_out, nand_4_out);
  nand nand_4 (nand_4_out, nand_3_out, not_2_out, D);
  nand nand_5 (Q, nand_2_out, nand_6_out);
  nand nand_6 (nand_6_out, Q, nand_3_out);
endmodule

module Exercicio_3 (
  input  in_1,
  input  Load,
  input  Clear,
  output out_4,
  output out_5,
  output out_6,
  output out_7,
  output out_8,
  output out_9,
  output out_10,
  output out_11
);

  wire clock_1_out;

  Clock clock_1 (.out(clock_1_out));
  Exercicio_2 exercicio_2_1 (.C(clock_1_out), .Clear(Clear), .D(out_4), .Q(out_5), .Load(Load));
  Exercicio_2 exercicio_2_2 (.C(clock_1_out), .Clear(Clear), .D(in_1), .Q(out_4), .Load(Load));
  Exercicio_2 exercicio_2_3 (.C(clock_1_out), .Clear(Clear), .D(out_5), .Q(out_6), .Load(Load));
  Exercicio_2 exercicio_2_4 (.C(clock_1_out), .Clear(Clear), .D(out_6), .Q(out_7), .Load(Load));
  Exercicio_2 exercicio_2_5 (.C(clock_1_out), .Clear(Clear), .D(out_7), .Q(out_8), .Load(Load));
  Exercicio_2 exercicio_2_6 (.C(clock_1_out), .Clear(Clear), .D(out_8), .Q(out_9), .Load(Load));
  Exercicio_2 exercicio_2_7 (.C(clock_1_out), .Clear(Clear), .D(out_9), .Q(out_10), .Load(Load));
  Exercicio_2 exercicio_2_8 (.C(clock_1_out), .Clear(Clear), .D(out_10), .Q(out_11), .Load(Load));
endmodule

module Exercicio_4 (
  input  Liga
);

  wire clock_1_out, Zera_out;
  wire [3:0] not_1_out, t_ff_1_q;

  Clock clock_1 (.out(clock_1_out));
  Button Zera (.out(Zera_out));
  T_Flip_Flop t_ff_1 (.clk(clock_1_out), .T(Liga), .Q(t_ff_1_q[0]), .preset(Zera_out));  // open: Qn, reset, en
  T_Flip_Flop t_ff_2 (.clk(t_ff_1_q[0]), .T(Liga), .Q(t_ff_1_q[1]), .preset(Zera_out));  // open: Qn, reset, en
  T_Flip_Flop t_ff_3 (.clk(t_ff_1_q[1]), .T(Liga), .Q(t_ff_1_q[2]), .preset(Zera_out));  // open: Qn, reset, en
  T_Flip_Flop t_ff_4 (.clk(t_ff_1_q[2]), .T(Liga), .Q(t_ff_1_q[3]), .preset(Zera_out));  // open: Qn, reset, en
  Hex_Digit_Display hex_digit_display_1 (.value(not_1_out));  // open: dp
  assign not_1_out = ~t_ff_1_q;  // NOT_Gate not_1, 4 bits wide
endmodule
