// Logisim project T24.circ as structural Verilog: 6 circuits, main circuit main
module main (
);


  // Notes on the sheet:
  //   Integrantes:
  //   Alexsander Luiz Gomes
  //   Rafael Nossal
  //   Pedro Grazziani Fernandes
endmodule

// REG 1 B
module Exercicio_2 (
  input  Load,
  input  C,
  input  Clear,
  input  D,
  output Q
);

  wire and_1_out, nand_1_out, nand_2_out, nand_3_out, nand_4_out, nand_6_out, not_1_out, not_2_out, or_1_out;

  and and_1 (and_1_out, Load, C);
  or or_1 (or_1_out, Clear, and_1_out);
  not not_1 (not_1_out, Clear);
  not not_2 (not_2_out, Clear);
  nand nand_1 (nand_1_out, nand_4_out, nand_2_out);
  nand nand_2 (nand_2_out, nand_1_out, not_1_out, and_1_out);
  nand nand_3 (nand_3_out, nand_2_out, or_1_out, nand_4_out);
  nand nand_4 (nand_4_out, nand_3_out, not_2_out, D);
  nand nand_5 (Q, nand_2_out, nand_6_out);
  nand nand_6 (nand_6_out, Q, nand_3_out);
endmodule

// REG 8 B
module Exercicio_3 (
  input  E,
  input  Load,
  input  Clear,
  output S7,
  output S6,
  output S5,
  output S4,
  output S3,
  output S2,
  output S1,
  output S0
);

  wire clock_1_out;

  Clock clock_1 (.out(clock_1_out));
  Exercicio_2 exercicio_2_1 (.C(clock_1_out), .Clear(Clear), .D(E), .Q(S7), .Load(Load));
  Exercicio_2 exercicio_2_2 (.C(clock_1_out), .Clear(Clear), .D(S7), .Q(S6), .Load(Load));
  Exercicio_2 exercicio_2_3 (.C(clock_1_out), .Clear(Clear), .D(S6), .Q(S5), .Load(Load));
  Exercicio_2 exercicio_2_4 (.C(clock_1_out), .Clear(Clear), .D(S5), .Q(S4), .Load(Load));
  Exercicio_2 exercicio_2_5 (.C(clock_1_out), .Clear(Clear), .D(S4), .Q(S3), .Load(Load));
  Exercicio_2 exercicio_2_6 (.C(clock_1_out), .Clear(Clear), .D(S3), .Q(S2), .Load(Load));
  Exercicio_2 exercicio_2_7 (.C(clock_1_out), .Clear(Clear), .D(S2), .Q(S1), .Load(Load));
  Exercicio_2 exercicio_2_8 (.C(clock_1_out), .Clear(Clear), .D(S1), .Q(S0), .Load(Load));
endmodule

module Exercicio_4 (
  input  Liga
);

  wire clock_1_out, Zera_out;
  wire [3:0] not_1_out, t_ff_1_q;

  Clock clock_1 (.out(clock_1_out));
  Button Zera (.out(Zera_out));
  T_Flip_Flop t_ff_1 (.clk(clock_1_out), .T(Liga), .Q(t_ff_1_q[0]), .preset(Zera_out));  // open: Qn, reset, en
  T_Flip_Flop t_ff_2 (.clk(t_ff_1_q[0]), .T(Liga), .Q(t_ff_1_q[1]), .preset(Zera_out));  // open: Qn, reset, en
  T_Flip_Flop t_ff_3 (.clk(t_ff_1_q[1]), .T(Liga), .Q(t_ff_1_q[2]), .preset(Zera_out));  // open: Qn, reset, en
  T_Flip_Flop t_ff_4 (.clk(t_ff_1_q[2]), .T(Liga), .Q(t_ff_1_q[3]), .preset(Zera_out));  // open: Qn, reset, en
  Hex_Digit_Display hex_digit_display_1 (.value(not_1_out));  // open: dp
  assign not_1_out = ~t_ff_1_q;  // NOT_Gate not_1, 4 bits wide
endmodule

module Exercicio_5 (
  input  Serial,
  input  Serial_Paralel,
  input  Load,
  input  Clear,
  input  P7,
  input  P6,
  input  P5,
  input  P4,
  input  P3,
  input  P2,
  input  P1,
  input  P0,
  output S7,
  output S6,
  output S5,
  output S4,
  output S3,
  output S2,
  output S1,
  output S0
);

  wire clock_1_out, mux_1_s, mux_2_s, mux_3_s, mux_4_s, mux_5_s, mux_6_s, mux_7_s, mux_8_s;

  Clock clock_1 (.out(clock_1_out));
  MUX mux_1 (.E0(Serial), .E1(P7), .A0(Serial_Paralel), .S(mux_1_s));
  Exercicio_2 exercicio_2_1 (.C(clock_1_out), .Clear(Clear), .D(mux_1_s), .Q(S7), .Load(Load));
  MUX mux_2 (.E0(S7), .E1(P6), .A0(Serial_Paralel), .S(mux_2_s));
  Exercicio_2 exercicio_2_2 (.C(clock_1_out), .Clear(Clear), .D(mux_2_s), .Q(S6), .Load(Load));
  MUX mux_3 (.E0(S6), .E1(P5), .A0(Serial_Paralel), .S(mux_3_s));
  Exercicio_2 exercicio_2_3 (.C(clock_1_out), .Clear(Clear), .D(mux_3_s), .Q(S5), .Load(Load));
  Exercicio_2 exercicio_2_4 (.C(clock_1_out), .Clear(Clear), .D(mux_4_s), .Q(S4), .Load(Load));
  MUX mux_4 (.E0(S5), .E1(P4), .A0(Serial_Paralel), .S(mux_4_s));
  MUX mux_5 (.E0(S4), .E1(P3), .A0(Serial_Paralel), .S(mux_5_s));
  Exercicio_2 exercicio_2_5 (.C(clock_1_out), .Clear(Clear), .D(mux_5_s), .Q(S3), .Load(Load));
  MUX mux_6 (.E0(S3), .E1(P2), .A0(Serial_Paralel), .S(mux_6_s));
  Exercicio_2 exercicio_2_6 (.C(clock_1_out), .Clear(Clear), .D(mux_6_s), .Q(S2), .Load(Load));
  MUX mux_7 (.E0(S2), .E1(P1), .A0(Serial_Paralel), .S(mux_7_s));
  Exercicio_2 exercicio_2_7 (.C(clock_1_out), .Clear(Clear), .D(mux_7_s), .Q(S1), .Load(Load));
  Exercicio_2 exercicio_2_8 (.C(clock_1_out), .Clear(Clear), .D(mux_8_s), .Q(S0), .Load(Load));
  MUX mux_8 (.E0(S1), .E1(P0), .A0(Serial_Paralel), .S(mux_8_s));
endmodule

module MUX (
  input  E0,
  input  E1,
  input  A0,
  output S
);

  wire and_1_out, and_2_out, not_1_out;

  not not_1 (not_1_out, A0);
  and and_1 (and_1_out, E0, not_1_out);
  and and_2 (and_2_out, E1, A0);
  or or_1 (S, and_1_out, and_2_out);
endmodule
