// Logisim project GabT13.circ as structural Verilog: 2 circuits, main circuit main
module main (
  input  P,
  input  A,
  input  B,
  input  C,
  input  SECRETARIO
);

  wire and_1_out, and_2_out, and_3_out, and_4_out, and_5_out, and_6_out, and_7_out, and_8_out, and_9_out,
       not_1_out, not_2_out, not_3_out, not_4_out, not_5_out, or_1_out, or_2_out;

  not not_1 (not_1_out, C);
  not not_2 (not_2_out, B);
  not not_3 (not_3_out, A);
  not not_4 (not_4_out, P);
  and and_1 (and_1_out, P, A);
  and and_2 (and_2_out, P, B);
  and and_3 (and_3_out, P, C);
  and and_4 (and_4_out, A, B, C);
  and and_5 (and_5_out, P, A, B, C);
  and and_6 (and_6_out, not_1_out, not_2_out, not_3_out, not_4_out);
  or or_1 (or_1_out, and_5_out, and_6_out);
  or or_2 (or_2_out, and_1_out, and_2_out, and_3_out, and_4_out);
  not not_5 (not_5_out, or_2_out);
  LED SIM (.in(and_7_out));
  and and_7 (and_7_out, or_2_out, SECRETARIO);
  LED NAO (.in(and_8_out));
  and and_8 (and_8_out, not_5_out, SECRETARIO);
  LED _4 (.in(and_9_out));
  and and_9 (and_9_out, SECRETARIO, or_1_out);

  // Notes on the sheet:
  //   CIRCUITO PARA O SIM
  //   CIRCUITO PARA O UNANIME
endmodule

module _2_e_3_votos (
  input  P,
  input  A,
  input  B,
  input  C,
  output V2,
  output V3
);

  wire and_1_out, and_2_out, and_3_out, and_4_out, and_5_out, and_6_out, and_7_out, and_8_out, and_9_out,
       and_10_out, and_11_out, and_12_out, and_13_out, and_14_out, not_1_out, not_2_out, not_3_out,
       not_4_out, not_5_out, not_6_out, not_7_out, not_8_out, not_9_out, not_10_out, not_11_out, not_12_out,
       not_13_out, not_14_out, not_15_out, not_16_out, not_17_out, not_18_out, not_19_out, not_20_out,
       not_21_out, not_22_out, not_23_out, not_24_out, not_25_out, not_26_out, not_27_out, not_28_out;

  not not_1 (not_1_out, P);
  not not_2 (not_2_out, A);
  not not_3 (not_3_out, P);
  not not_4 (not_4_out, B);
  not not_5 (not_5_out, P);
  not not_6 (not_6_out, C);
  not not_7 (not_7_out, A);
  not not_8 (not_8_out, B);
  not not_9 (not_9_out, A);
  not not_10 (not_10_out, C);
  not not_11 (not_11_out, B);
  not not_12 (not_12_out, C);
  not not_13 (not_13_out, P);
  not not_14 (not_14_out, A);
  not not_15 (not_15_out, B);
  not not_16 (not_16_out, P);
  not not_17 (not_17_out, A);
  not not_18 (not_18_out, C);
  not not_19 (not_19_out, P);
  not not_20 (not_20_out, B);
  not not_21 (not_21_out, C);
  not not_22 (not_22_out, P);
  not not_23 (not_23_out, A);
  not not_24 (not_24_out, B);
  not not_25 (not_25_out, C);
  not not_26 (not_26_out, A);
  not not_27 (not_27_out, B);
  not not_28 (not_28_out, C);
  and and_1 (and_1_out, not_1_out, not_2_out, B, C);
  and and_2 (and_2_out, not_3_out, A, not_4_out, C);
  and and_3 (and_3_out, not_5_out, A, B, not_6_out);
  and and_4 (and_4_out, P, not_7_out, not_8_out, C);
  and and_5 (and_5_out, P, not_9_out, B, not_10_out);
  and and_6 (and_6_out, P, A, not_11_out, not_12_out);
  and and_7 (and_7_out, not_13_out, not_14_out, not_15_out, C);
  and and_8 (and_8_out, not_16_out, not_17_out, B, not_18_out);
  and and_9 (and_9_out, not_19_out, A, not_20_out, not_21_out);
  and and_10 (and_10_out, not_22_out, A, B, C);
  and and_11 (and_11_out, P, not_23_out, not_24_out, not_25_out);
  and and_12 (and_12_out, P, not_26_out, B, C);
  and and_13 (and_13_out, P, A, not_27_out, C);
  and and_14 (and_14_out, P, A, B, not_28_out);
  or or_1 (V2, and_1_out, and_2_out, and_3_out, and_4_out, and_5_out, and_6_out);
  or or_2 (V3, and_7_out, and_8_out, and_9_out, and_10_out, and_11_out, and_12_out, and_13_out, and_14_out);
endmodule
