// Logisim project RespT14.circ as structural Verilog: 3 circuits, main circuit Questao A
module Questao_A (
  input  A,
  input  B,
  output S
);

  wire and_1_out, and_2_out, not_1_out, not_2_out, xor_1_out;

  not not_1 (not_1_out, B);
  and and_1 (and_1_out, A, not_1_out);
  not not_2 (not_2_out, A);
  and and_2 (and_2_out, not_2_out, B);
  xor xor_1 (xor_1_out, B, A);
  or or_1 (S, and_1_out, and_2_out);
  LED Lampada (.in(S));
  LED Lampada_2 (.in(xor_1_out));

  // Notes on the sheet:
  //   Circuito a partir da tabela verdade
  //   Circuito usando XOR
endmodule

module Questao_B (
  input  A,
  input  B,
  input  C,
  output S
);

  wire xor_1_out;

  xor xor_1 (xor_1_out, A, B);
  xor xor_2 (S, xor_1_out, C);
  LED Lampada (.in(S));

  // Notes on the sheet:
  //   Usando XOR simplesmente dava
  //   Mas quem fez tabela verdade e mapa tambem deve funcionar
endmodule

module Questao_C (
  input  A,
  input  B,
  input  C,
  input  D,
  output S1,
  output S2
);

  wire and_1_out, and_2_out, and_3_out, and_4_out, and_5_out, and_6_out, xor_1_out, xor_2_out;

  xor xor_1 (xor_1_out, B, C);
  and and_1 (and_1_out, ~A, ~B, C, D);  // AND_Gate
  and and_2 (and_2_out, ~A, B, ~C, D);  // AND_Gate
  and and_3 (and_3_out, ~A, B, C, ~D);  // AND_Gate
  and and_4 (and_4_out, A, ~B, ~C, D);  // AND_Gate
  and and_5 (and_5_out, A, ~B, C, ~D);  // AND_Gate
  and and_6 (and_6_out, A, B, ~C, ~D);  // AND_Gate
  xor xor_2 (xor_2_out, xor_1_out, D);
  or or_1 (S1, xor_2_out, A);
  or or_2 (S2, and_1_out, and_2_out, and_3_out, and_4_out, and_5_out, and_6_out);
  LED Lampada (.in(S1));
  LED Lampada_2 (.in(S2));

  // Notes on the sheet:
  //   A mantem ligado sempre
  //   A em 0, B C D em Hotel
  //   Dois ligados acente
  //   Mas somente dois
endmodule
