// Logisim project T15-4.circ as structural Verilog: 1 circuit, main circuit main
module main (
  input  B0,
  input  B1,
  input  B2,
  input  B3,
  input  B4,
  input  B5,
  input  B6,
  input  B7
);

  wire xor_1_out, xor_2_out, xor_3_out, xor_4_out, xor_5_out, xor_6_out, xor_7_out;

  xor xor_1 (xor_1_out, B0, B1);
  xor xor_2 (xor_2_out, xor_1_out, B2);
  xor xor_3 (xor_3_out, xor_2_out, B3);
  xor xor_4 (xor_4_out, xor_3_out, B4);
  xor xor_5 (xor_5_out, xor_4_out, B5);
  xor xor_6 (xor_6_out, xor_5_out, B6);
  xor xor_7 (xor_7_out, xor_6_out, B7);
  LED led_1 (.in(xor_7_out));

  // Notes on the sheet:
  //   ERRO!
endmodule
