// Logisim project T16 - 1 - A.circ as structural Verilog: 1 circuit, main circuit main
module main (
  input  E1,
  input  E2,
  input  E3,
  input  E4,
  input  H
);

  wire and_1_out, and_2_out, and_3_out, and_4_out, and_5_out, and_6_out, and_7_out, and_8_out, and_9_out,
       and_10_out, and_11_out, and_12_out, and_13_out, and_14_out, and_15_out, and_16_out, not_1_out,
       not_2_out, not_3_out, not_4_out;

  not not_1 (not_1_out, E1);
  not not_2 (not_2_out, E2);
  not not_3 (not_3_out, E3);
  not not_4 (not_4_out, E4);
  and and_1 (and_1_out, H, E4, E3, E2, E1);
  and and_2 (and_2_out, H, not_4_out, E3, E2, E1);
  and and_3 (and_3_out, H, E4, not_3_out, E2, E1);
  and and_4 (and_4_out, H, not_4_out, not_3_out, E2, E1);
  and and_5 (and_5_out, H, E4, E3, not_2_out, E1);
  and and_6 (and_6_out, H, not_4_out, E3, not_2_out, E1);
  and and_7 (and_7_out, H, not_4_out, not_3_out, not_2_out, E1);
  and and_8 (and_8_out, H, E4, not_3_out, not_2_out, E1);
  and and_9 (and_9_out, H, E4, E3, E2, not_1_out);
  and and_10 (and_10_out, H, not_4_out, E3, E2, not_1_out);
  and and_11 (and_11_out, H, not_4_out, not_3_out, E2, not_1_out);
  and and_12 (and_12_out, H, E4, not_3_out, E2, not_1_out);
  and and_13 (and_13_out, H, E4, E3, not_2_out, not_1_out);
  and and_14 (and_14_out, H, not_4_out, E3, not_2_out, not_1_out);
  and and_15 (and_15_out, H, E4, not_3_out, not_2_out, not_1_out);
  and and_16 (and_16_out, H, not_4_out, not_3_out, not_2_out, not_1_out);

  // Notes on the sheet:
  //   S15
  //   S14
  //   S13
  //   S12
  //   S11
  //   S10
  //   S9
  //   S8
  //   S7
  //   S5
  //   S6
  //   S4
  //   S3
  //   S1
  //   S2
  //   S0
endmodule
