// Logisim project T16 - 1 - C.circ as structural Verilog: 1 circuit, main circuit main
module main (
  input  E0,
  input  C0,
  input  C1,
  input  C2,
  input  H
);

  wire and_1_out, and_2_out, and_3_out, and_4_out, and_5_out, and_6_out, and_7_out, and_8_out, not_1_out,
       not_2_out, not_3_out;

  not not_1 (not_1_out, C0);
  not not_2 (not_2_out, C1);
  not not_3 (not_3_out, C2);
  and and_1 (and_1_out, E0, not_1_out, not_2_out, not_3_out, H);
  and and_2 (and_2_out, E0, not_1_out, not_2_out, C2, H);
  and and_3 (and_3_out, E0, not_1_out, C1, not_3_out, H);
  and and_4 (and_4_out, E0, not_1_out, C1, C2, H);
  and and_5 (and_5_out, E0, C0, not_2_out, not_3_out, H);
  and and_6 (and_6_out, E0, C0, not_2_out, C2, H);
  and and_7 (and_7_out, E0, C0, C1, not_3_out, H);
  and and_8 (and_8_out, E0, C0, C1, C2, H);

  // Notes on the sheet:
  //   S0
  //   S1
  //   S2
  //   S3
  //   S4
  //   S5
  //   S6
  //   S7
endmodule
